// Logisim project ULA.circ as structural Verilog: 8 circuits, main circuit main
module main (
  input  [15:0] x,
  input  [15:0] y,
  input  [6:0] zxnxzynyfincno,
  output [15:0] outp,
  output zr,
  output ng,
  output overflow
);

  wire or16way_1_out_2;
  wire [15:0] and_1_out, and_2_out, and_3_out, multiplexer_1_out, multiplexer_2_out, multiplexer_3_out,
       multiplexer_4_out, multiplexer_5_out, not_1_out, not_2_out, not_3_out, not_4_out, not_5_out,
       sixteenbitadder_1_out_4;

  assign not_1_out = ~x;  // NOT_Gate not_1, 16 bits wide
  assign not_2_out = ~y;  // NOT_Gate not_2, 16 bits wide
  assign and_1_out = not_1_out & x;  // AND_Gate and_1, 16 bits wide
  assign and_2_out = not_2_out & y;  // AND_Gate and_2, 16 bits wide
  Multiplexer #(.width(16)) multiplexer_1 (.in0(x), .in1(and_1_out), .out(multiplexer_1_out), .sel(zxnxzynyfincno[6]));
  Multiplexer #(.width(16)) multiplexer_2 (.in0(y), .in1(and_2_out), .out(multiplexer_2_out), .sel(zxnxzynyfincno[4]));
  Multiplexer #(.width(16)) multiplexer_3 (
    .in0(multiplexer_1_out), .in1(not_3_out), .out(multiplexer_3_out), .sel(zxnxzynyfincno[5]));
  assign not_3_out = ~multiplexer_1_out;  // NOT_Gate not_3, 16 bits wide
  Multiplexer #(.width(16)) multiplexer_4 (
    .in0(multiplexer_2_out), .in1(not_4_out), .out(multiplexer_4_out), .sel(zxnxzynyfincno[3]));
  assign not_4_out = ~multiplexer_2_out;  // NOT_Gate not_4, 16 bits wide
  assign and_3_out = multiplexer_3_out & multiplexer_4_out;  // AND_Gate and_3, 16 bits wide
  Multiplexer #(.width(16)) multiplexer_5 (
    .in0(and_3_out), .in1(sixteenbitadder_1_out_4), .out(multiplexer_5_out), .sel(zxnxzynyfincno[2]));
  SixteenBitAdder sixteenbitadder_1 (
    .cin(zxnxzynyfincno[1]), .in_2(multiplexer_3_out), .in_3(multiplexer_4_out),
    .out_4(sixteenbitadder_1_out_4), .cout(overflow));
  Multiplexer #(.width(16)) multiplexer_6 (
    .in0(multiplexer_5_out), .in1(not_5_out), .out({ng, outp[14:0]}), .sel(zxnxzynyfincno[0]));
  assign not_5_out = ~multiplexer_5_out;  // NOT_Gate not_5, 16 bits wide
  Or16Way or16way_1 (.in_1({ng, outp[14:0]}), .out_2(or16way_1_out_2));
  not not_6 (zr, or16way_1_out_2);

  assign outp[15] = ng;
endmodule

module Or16Way (
  input  [15:0] in_1,
  output out_2
);

  or or_1 (out_2, in_1[0], in_1[1], in_1[2], in_1[3], in_1[4], in_1[5], in_1[6], in_1[7], in_1[8], in_1[9], in_1[10], in_1[11], in_1[12], in_1[13], in_1[14], in_1[15]);
endmodule

module FourBitAdder (
  input  cin,
  input  inputA0,
  input  inputB0,
  input  inputA1,
  input  inputB1,
  input  inputA2,
  input  inputB2,
  input  inputA3,
  input  inputB3,
  output outputsS0,
  output outputS1,
  output outputS2,
  output outputS3,
  output cout
);

  wire twobitadder_1_cout;

  TwoBitAdder twobitadder_1 (
    .cin(cin), .inputA0(inputA0), .inputB0(inputB0), .inputA1(inputA1), .inputB1(inputB1),
    .outputS0(outputsS0), .outputS1(outputS1), .cout(twobitadder_1_cout));
  TwoBitAdder twobitadder_2 (
    .cin(twobitadder_1_cout), .inputA0(inputA2), .inputB0(inputB2), .inputA1(inputA3), .inputB1(inputB3),
    .outputS0(outputS2), .outputS1(outputS3), .cout(cout));
endmodule

module HalfAdder (
  input  inputA0,
  input  inputB0,
  output outputS0,
  output cout
);

  xor xor_1 (outputS0, inputA0, inputB0);
  and and_1 (cout, inputA0, inputB0);

  // Notes on the sheet:
  //   S0
  //   V0
endmodule

module TwoBitAdder (
  input  cin,
  input  inputA0,
  input  inputB0,
  input  inputA1,
  input  inputB1,
  output outputS0,
  output outputS1,
  output cout
);

  wire fulladder_1_cout;

  FullAdder fulladder_1 (
    .cin(cin), .inputA0(inputA0), .inputB0(inputB0), .outputsS0(outputS0), .cout(fulladder_1_cout));
  FullAdder fulladder_2 (
    .cin(fulladder_1_cout), .inputA0(inputA1), .inputB0(inputB1), .outputsS0(outputS1), .cout(cout));
endmodule

module FullAdder (
  input  cin,
  input  inputA0,
  input  inputB0,
  output outputsS0,
  output cout
);

  wire halfadder_1_cout, halfadder_1_outputs0, halfadder_2_cout;

  HalfAdder halfadder_1 (
    .inputA0(inputA0), .inputB0(inputB0), .outputS0(halfadder_1_outputs0), .cout(halfadder_1_cout));
  HalfAdder halfadder_2 (.inputA0(cin), .inputB0(halfadder_1_outputs0), .outputS0(outputsS0), .cout(halfadder_2_cout));
  or or_1 (cout, halfadder_2_cout, halfadder_1_cout);
endmodule

module EightBitAdder (
  input  cin,
  input  inputA0,
  input  inputB0,
  input  inputA1,
  input  inputB1,
  input  inputA2,
  input  inputB2,
  input  inputA3,
  input  inputB3,
  input  inputA4,
  input  inputB4,
  input  inputA5,
  input  inputB5,
  input  inputA6,
  input  inputB6,
  input  inputA7,
  input  inputB7,
  output outputsS0,
  output outputS1,
  output outputS2,
  output outputS3,
  output outputsS4,
  output outputsS5,
  output outputsS6,
  output outputsS7,
  output cout
);

  wire fourbitadder_1_cout;

  FourBitAdder fourbitadder_1 (
    .cin(cin), .inputA0(inputA0), .inputB0(inputB0), .inputA1(inputA1), .inputB1(inputB1), .inputA2(inputA2),
    .inputB2(inputB2), .inputA3(inputA3), .inputB3(inputB3), .outputsS0(outputsS0), .outputS1(outputS1),
    .outputS2(outputS2), .outputS3(outputS3), .cout(fourbitadder_1_cout));
  FourBitAdder fourbitadder_2 (
    .cin(fourbitadder_1_cout), .inputA0(inputA4), .inputB0(inputB4), .inputA1(inputA5), .inputB1(inputB5),
    .inputA2(inputA6), .inputB2(inputB6), .inputA3(inputA7), .inputB3(inputB7), .outputsS0(outputsS4),
    .outputS1(outputsS5), .outputS2(outputsS6), .outputS3(outputsS7), .cout(cout));
endmodule

module SixteenBitAdder (
  input  cin,
  input  [15:0] in_2,
  input  [15:0] in_3,
  output [15:0] out_4,
  output cout
);

  wire eightbitadder_1_cout;

  EightBitAdder eightbitadder_1 (
    .cin(cin), .inputA0(in_2[0]), .inputB0(in_3[0]), .inputA1(in_2[1]), .inputB1(in_3[1]), .inputA2(in_2[2]),
    .inputB2(in_3[2]), .inputA3(in_2[3]), .inputB3(in_3[3]), .inputA4(in_2[4]), .inputB4(in_3[4]),
    .inputA5(in_2[5]), .inputB5(in_3[5]), .inputA6(in_2[6]), .inputB6(in_3[6]), .inputA7(in_2[7]),
    .inputB7(in_3[7]), .outputsS0(out_4[0]), .outputS1(out_4[1]), .outputS2(out_4[2]), .outputS3(out_4[3]),
    .outputsS4(out_4[4]), .outputsS5(out_4[5]), .outputsS6(out_4[6]), .outputsS7(out_4[7]),
    .cout(eightbitadder_1_cout));
  EightBitAdder eightbitadder_2 (
    .cin(eightbitadder_1_cout), .inputA0(in_2[8]), .inputB0(in_3[8]), .inputA1(in_2[9]), .inputB1(in_3[9]),
    .inputA2(in_2[10]), .inputB2(in_3[10]), .inputA3(in_2[11]), .inputB3(in_3[11]), .inputA4(in_2[12]),
    .inputB4(in_3[12]), .inputA5(in_2[13]), .inputB5(in_3[13]), .inputA6(in_2[14]), .inputB6(in_3[14]),
    .inputA7(in_2[15]), .inputB7(in_3[15]), .outputsS0(out_4[8]), .outputS1(out_4[9]), .outputS2(out_4[10]),
    .outputS3(out_4[11]), .outputsS4(out_4[12]), .outputsS5(out_4[13]), .outputsS6(out_4[14]),
    .outputsS7(out_4[15]), .cout(cout));
endmodule
