// Logisim project Computer.circ as structural Verilog: 22 circuits, main circuit main
module main (
  input  reset,
  input  [15:0] keyboard
);

  wire cpu_1_clockout, cpu_1_writem;
  wire [15:0] cpu_1_addressm, cpu_1_outm, cpu_1_pcc, memory_1_outt, rom_1_data;

  ROM #(.addrWidth(16), .dataWidth(16)) rom_1 (.addr(cpu_1_pcc), .data(rom_1_data));
  CPU cpu_1 (
    .instruction(rom_1_data), .inM(memory_1_outt), .reset(reset), .outM(cpu_1_outm), .writeM(cpu_1_writem),
    .addressM(cpu_1_addressm), .pcc(cpu_1_pcc), .clockOut(cpu_1_clockout));
  Memory memory_1 (
    .load(cpu_1_writem), .inpt(cpu_1_outm), .address(cpu_1_addressm[14:0]), .clock(cpu_1_clockout),
    .keyboard(keyboard), .outt(memory_1_outt));
endmodule

module Or16Way (
  input  [15:0] in_1,
  output out_2
);

  or or_1 (out_2, in_1[0], in_1[1], in_1[2], in_1[3], in_1[4], in_1[5], in_1[6], in_1[7], in_1[8], in_1[9], in_1[10], in_1[11], in_1[12], in_1[13], in_1[14], in_1[15]);
endmodule

module HalfAdder (
  input  inputA0,
  input  inputB0,
  output outputS0,
  output cout
);

  xor xor_1 (outputS0, inputA0, inputB0);
  and and_1 (cout, inputA0, inputB0);

  // Notes on the sheet:
  //   S0
  //   V0
endmodule

module FullAdder (
  input  cin,
  input  inputA0,
  input  inputB0,
  output outputsS0,
  output cout
);

  wire halfadder_1_cout, halfadder_1_outputs0, halfadder_2_cout;

  HalfAdder halfadder_1 (
    .inputA0(inputA0), .inputB0(inputB0), .outputS0(halfadder_1_outputs0), .cout(halfadder_1_cout));
  HalfAdder halfadder_2 (.inputA0(cin), .inputB0(halfadder_1_outputs0), .outputS0(outputsS0), .cout(halfadder_2_cout));
  or or_1 (cout, halfadder_2_cout, halfadder_1_cout);
endmodule

module TwoBitAdder (
  input  cin,
  input  inputA0,
  input  inputB0,
  input  inputA1,
  input  inputB1,
  output outputS0,
  output outputS1,
  output cout
);

  wire fulladder_1_cout;

  FullAdder fulladder_1 (
    .cin(cin), .inputA0(inputA0), .inputB0(inputB0), .outputsS0(outputS0), .cout(fulladder_1_cout));
  FullAdder fulladder_2 (
    .cin(fulladder_1_cout), .inputA0(inputA1), .inputB0(inputB1), .outputsS0(outputS1), .cout(cout));
endmodule

module FourBitAdder (
  input  cin,
  input  inputA0,
  input  inputB0,
  input  inputA1,
  input  inputB1,
  input  inputA2,
  input  inputB2,
  input  inputA3,
  input  inputB3,
  output outputsS0,
  output outputS1,
  output outputS2,
  output outputS3,
  output cout
);

  wire twobitadder_1_cout;

  TwoBitAdder twobitadder_1 (
    .cin(cin), .inputA0(inputA0), .inputB0(inputB0), .inputA1(inputA1), .inputB1(inputB1),
    .outputS0(outputsS0), .outputS1(outputS1), .cout(twobitadder_1_cout));
  TwoBitAdder twobitadder_2 (
    .cin(twobitadder_1_cout), .inputA0(inputA2), .inputB0(inputB2), .inputA1(inputA3), .inputB1(inputB3),
    .outputS0(outputS2), .outputS1(outputS3), .cout(cout));
endmodule

module EightBitAdder (
  input  cin,
  input  inputA0,
  input  inputB0,
  input  inputA1,
  input  inputB1,
  input  inputA2,
  input  inputB2,
  input  inputA3,
  input  inputB3,
  input  inputA4,
  input  inputB4,
  input  inputA5,
  input  inputB5,
  input  inputA6,
  input  inputB6,
  input  inputA7,
  input  inputB7,
  output outputsS0,
  output outputS1,
  output outputS2,
  output outputS3,
  output outputsS4,
  output outputsS5,
  output outputsS6,
  output outputsS7,
  output cout
);

  wire fourbitadder_1_cout;

  FourBitAdder fourbitadder_1 (
    .cin(cin), .inputA0(inputA0), .inputB0(inputB0), .inputA1(inputA1), .inputB1(inputB1), .inputA2(inputA2),
    .inputB2(inputB2), .inputA3(inputA3), .inputB3(inputB3), .outputsS0(outputsS0), .outputS1(outputS1),
    .outputS2(outputS2), .outputS3(outputS3), .cout(fourbitadder_1_cout));
  FourBitAdder fourbitadder_2 (
    .cin(fourbitadder_1_cout), .inputA0(inputA4), .inputB0(inputB4), .inputA1(inputA5), .inputB1(inputB5),
    .inputA2(inputA6), .inputB2(inputB6), .inputA3(inputA7), .inputB3(inputB7), .outputsS0(outputsS4),
    .outputS1(outputsS5), .outputS2(outputsS6), .outputS3(outputsS7), .cout(cout));
endmodule

module SixteenBitAdder (
  input  cin,
  input  [15:0] x,
  input  [15:0] y,
  output [15:0] outp,
  output cout
);

  wire eightbitadder_1_cout;

  EightBitAdder eightbitadder_1 (
    .cin(cin), .inputA0(x[0]), .inputB0(y[0]), .inputA1(x[1]), .inputB1(y[1]), .inputA2(x[2]),
    .inputB2(y[2]), .inputA3(x[3]), .inputB3(y[3]), .inputA4(x[4]), .inputB4(y[4]), .inputA5(x[5]),
    .inputB5(y[5]), .inputA6(x[6]), .inputB6(y[6]), .inputA7(x[7]), .inputB7(y[7]), .outputsS0(outp[0]),
    .outputS1(outp[1]), .outputS2(outp[2]), .outputS3(outp[3]), .outputsS4(outp[4]), .outputsS5(outp[5]),
    .outputsS6(outp[6]), .outputsS7(outp[7]), .cout(eightbitadder_1_cout));
  EightBitAdder eightbitadder_2 (
    .cin(eightbitadder_1_cout), .inputA0(x[8]), .inputB0(y[8]), .inputA1(x[9]), .inputB1(y[9]),
    .inputA2(x[10]), .inputB2(y[10]), .inputA3(x[11]), .inputB3(y[11]), .inputA4(x[12]), .inputB4(y[12]),
    .inputA5(x[13]), .inputB5(y[13]), .inputA6(x[14]), .inputB6(y[14]), .inputA7(x[15]), .inputB7(y[15]),
    .outputsS0(outp[8]), .outputS1(outp[9]), .outputS2(outp[10]), .outputS3(outp[11]), .outputsS4(outp[12]),
    .outputsS5(outp[13]), .outputsS6(outp[14]), .outputsS7(outp[15]), .cout(cout));
endmodule

module ULA (
  input  [15:0] x,
  input  [15:0] y,
  input  zx,
  input  nx,
  input  zy,
  input  ny,
  input  f,
  input  no,
  output [15:0] outp,
  output zr,
  output ng,
  output overflow
);

  wire or16way_1_out_2;
  wire [15:0] and_1_out, and_2_out, and_3_out, multiplexer_1_out, multiplexer_2_out, multiplexer_3_out,
       multiplexer_4_out, multiplexer_5_out, not_1_out, not_2_out, not_3_out, not_4_out, not_5_out,
       sixteenbitadder_1_outp;

  assign not_1_out = ~x;  // NOT_Gate not_1, 16 bits wide
  assign not_2_out = ~y;  // NOT_Gate not_2, 16 bits wide
  assign and_1_out = not_1_out & x;  // AND_Gate and_1, 16 bits wide
  assign and_2_out = not_2_out & y;  // AND_Gate and_2, 16 bits wide
  Multiplexer #(.width(16)) multiplexer_1 (.in0(x), .in1(and_1_out), .out(multiplexer_1_out), .sel(zx));
  Multiplexer #(.width(16)) multiplexer_2 (.in0(y), .in1(and_2_out), .out(multiplexer_2_out), .sel(zy));
  Multiplexer #(.width(16)) multiplexer_3 (.in0(multiplexer_1_out), .in1(not_3_out), .out(multiplexer_3_out), .sel(nx));
  assign not_3_out = ~multiplexer_1_out;  // NOT_Gate not_3, 16 bits wide
  Multiplexer #(.width(16)) multiplexer_4 (.in0(multiplexer_2_out), .in1(not_4_out), .out(multiplexer_4_out), .sel(ny));
  assign not_4_out = ~multiplexer_2_out;  // NOT_Gate not_4, 16 bits wide
  assign and_3_out = multiplexer_3_out & multiplexer_4_out;  // AND_Gate and_3, 16 bits wide
  Multiplexer #(.width(16)) multiplexer_5 (
    .in0(and_3_out), .in1(sixteenbitadder_1_outp), .out(multiplexer_5_out), .sel(f));
  SixteenBitAdder sixteenbitadder_1 (
    .x(multiplexer_3_out), .y(multiplexer_4_out), .outp(sixteenbitadder_1_outp), .cout(overflow));  // open: cin
  Multiplexer #(.width(16)) multiplexer_6 (.in0(multiplexer_5_out), .in1(not_5_out), .out({ng, outp[14:0]}), .sel(no));
  assign not_5_out = ~multiplexer_5_out;  // NOT_Gate not_5, 16 bits wide
  Or16Way or16way_1 (.in_1({ng, outp[14:0]}), .out_2(or16way_1_out_2));
  not not_6 (zr, or16way_1_out_2);

  assign outp[15] = ng;
endmodule

module DFF (
  input  DFF_in,
  input  DFF_clk,
  input  DFF_load,
  output DFF_out,
  output DFF_out_c
);

  wire nand_1_out, nand_2_out;

  nand nand_1 (nand_1_out, DFF_in, DFF_clk);
  nand nand_2 (nand_2_out, DFF_clk, DFF_load);
  nand nand_3 (DFF_out, nand_1_out, DFF_out_c);
  nand nand_4 (DFF_out_c, DFF_out, nand_2_out);
endmodule

module RAM8 (
  input  clock,
  input  load,
  input  [2:0] address,
  input  [15:0] inpt,
  output [15:0] out_5
);

  wire demultiplexer_1_out0, demultiplexer_1_out1, demultiplexer_1_out2, demultiplexer_1_out3,
       demultiplexer_1_out4, demultiplexer_1_out5, demultiplexer_1_out6, demultiplexer_1_out7;
  wire [15:0] registerr_1_registerout, registerr_2_registerout, registerr_3_registerout,
       registerr_4_registerout, registerr_5_registerout, registerr_6_registerout, registerr_7_registerout,
       registerr_8_registerout;

  Demultiplexer #(.select(3)) demultiplexer_1 (
    .out0(demultiplexer_1_out0), .out1(demultiplexer_1_out1), .out2(demultiplexer_1_out2),
    .out3(demultiplexer_1_out3), .out4(demultiplexer_1_out4), .out5(demultiplexer_1_out5),
    .out6(demultiplexer_1_out6), .out7(demultiplexer_1_out7), .in(load), .sel(address));
  Registerr registerr_1 (
    .RegisterClock(clock), .RegisterLoad(demultiplexer_1_out0), .RegisterIn(inpt),
    .RegisterOut(registerr_1_registerout));
  Registerr registerr_2 (
    .RegisterClock(clock), .RegisterLoad(demultiplexer_1_out1), .RegisterIn(inpt),
    .RegisterOut(registerr_2_registerout));
  Registerr registerr_3 (
    .RegisterClock(clock), .RegisterLoad(demultiplexer_1_out2), .RegisterIn(inpt),
    .RegisterOut(registerr_3_registerout));
  Registerr registerr_4 (
    .RegisterClock(clock), .RegisterLoad(demultiplexer_1_out3), .RegisterIn(inpt),
    .RegisterOut(registerr_4_registerout));
  Registerr registerr_5 (
    .RegisterClock(clock), .RegisterLoad(demultiplexer_1_out4), .RegisterIn(inpt),
    .RegisterOut(registerr_5_registerout));
  Registerr registerr_6 (
    .RegisterClock(clock), .RegisterLoad(demultiplexer_1_out5), .RegisterIn(inpt),
    .RegisterOut(registerr_6_registerout));
  Registerr registerr_7 (
    .RegisterClock(clock), .RegisterLoad(demultiplexer_1_out6), .RegisterIn(inpt),
    .RegisterOut(registerr_7_registerout));
  Registerr registerr_8 (
    .RegisterClock(clock), .RegisterLoad(demultiplexer_1_out7), .RegisterIn(inpt),
    .RegisterOut(registerr_8_registerout));
  Multiplexer #(.select(3), .width(16)) multiplexer_1 (
    .in0(registerr_1_registerout), .in1(registerr_2_registerout), .in2(registerr_3_registerout),
    .in3(registerr_4_registerout), .in4(registerr_5_registerout), .in5(registerr_6_registerout),
    .in6(registerr_7_registerout), .in7(registerr_8_registerout), .out(out_5), .sel(address));
endmodule

module Registerr (
  input  RegisterClock,
  input  RegisterLoad,
  input  [15:0] RegisterIn,
  output [15:0] RegisterOut
);

  DFF dff_1 (
    .DFF_in(RegisterIn[0]), .DFF_clk(RegisterClock), .DFF_load(RegisterLoad), .DFF_out(RegisterOut[0]));  // open: DFF_out_c
  DFF dff_2 (
    .DFF_in(RegisterIn[1]), .DFF_clk(RegisterClock), .DFF_load(RegisterLoad), .DFF_out(RegisterOut[1]));  // open: DFF_out_c
  DFF dff_3 (
    .DFF_in(RegisterIn[2]), .DFF_clk(RegisterClock), .DFF_load(RegisterLoad), .DFF_out(RegisterOut[2]));  // open: DFF_out_c
  DFF dff_4 (
    .DFF_in(RegisterIn[3]), .DFF_clk(RegisterClock), .DFF_load(RegisterLoad), .DFF_out(RegisterOut[3]));  // open: DFF_out_c
  DFF dff_5 (
    .DFF_in(RegisterIn[4]), .DFF_clk(RegisterClock), .DFF_load(RegisterLoad), .DFF_out(RegisterOut[4]));  // open: DFF_out_c
  DFF dff_6 (
    .DFF_in(RegisterIn[5]), .DFF_clk(RegisterClock), .DFF_load(RegisterLoad), .DFF_out(RegisterOut[5]));  // open: DFF_out_c
  DFF dff_7 (
    .DFF_in(RegisterIn[6]), .DFF_clk(RegisterClock), .DFF_load(RegisterLoad), .DFF_out(RegisterOut[6]));  // open: DFF_out_c
  DFF dff_8 (
    .DFF_in(RegisterIn[7]), .DFF_clk(RegisterClock), .DFF_load(RegisterLoad), .DFF_out(RegisterOut[7]));  // open: DFF_out_c
  DFF dff_9 (
    .DFF_in(RegisterIn[8]), .DFF_clk(RegisterClock), .DFF_load(RegisterLoad), .DFF_out(RegisterOut[8]));  // open: DFF_out_c
  DFF dff_10 (
    .DFF_in(RegisterIn[9]), .DFF_clk(RegisterClock), .DFF_load(RegisterLoad), .DFF_out(RegisterOut[9]));  // open: DFF_out_c
  DFF dff_11 (
    .DFF_in(RegisterIn[10]), .DFF_clk(RegisterClock), .DFF_load(RegisterLoad), .DFF_out(RegisterOut[10]));  // open: DFF_out_c
  DFF dff_12 (
    .DFF_in(RegisterIn[11]), .DFF_clk(RegisterClock), .DFF_load(RegisterLoad), .DFF_out(RegisterOut[11]));  // open: DFF_out_c
  DFF dff_13 (
    .DFF_in(RegisterIn[12]), .DFF_clk(RegisterClock), .DFF_load(RegisterLoad), .DFF_out(RegisterOut[12]));  // open: DFF_out_c
  DFF dff_14 (
    .DFF_in(RegisterIn[13]), .DFF_clk(RegisterClock), .DFF_load(RegisterLoad), .DFF_out(RegisterOut[13]));  // open: DFF_out_c
  DFF dff_15 (
    .DFF_in(RegisterIn[14]), .DFF_clk(RegisterClock), .DFF_load(RegisterLoad), .DFF_out(RegisterOut[14]));  // open: DFF_out_c
  DFF dff_16 (
    .DFF_in(RegisterIn[15]), .DFF_clk(RegisterClock), .DFF_load(RegisterLoad), .DFF_out(RegisterOut[15]));  // open: DFF_out_c
endmodule

module RAM64 (
  input  clock,
  input  load,
  input  [5:0] address,
  input  [15:0] inpt,
  output [15:0] outp
);

  wire demultiplexer_1_out0, demultiplexer_1_out1, demultiplexer_1_out2, demultiplexer_1_out3,
       demultiplexer_1_out4, demultiplexer_1_out5, demultiplexer_1_out6, demultiplexer_1_out7;
  wire [15:0] ram8_1_out_5, ram8_2_out_5, ram8_3_out_5, ram8_4_out_5, ram8_5_out_5, ram8_6_out_5,
       ram8_7_out_5, ram8_8_out_5;

  Demultiplexer #(.select(3)) demultiplexer_1 (
    .out0(demultiplexer_1_out0), .out1(demultiplexer_1_out1), .out2(demultiplexer_1_out2),
    .out3(demultiplexer_1_out3), .out4(demultiplexer_1_out4), .out5(demultiplexer_1_out5),
    .out6(demultiplexer_1_out6), .out7(demultiplexer_1_out7), .in(load), .sel(address[5:3]));
  RAM8 ram8_1 (.clock(clock), .load(demultiplexer_1_out0), .address(address[2:0]), .inpt(inpt), .out_5(ram8_1_out_5));
  RAM8 ram8_2 (.clock(clock), .load(demultiplexer_1_out1), .address(address[2:0]), .inpt(inpt), .out_5(ram8_2_out_5));
  RAM8 ram8_3 (.clock(clock), .load(demultiplexer_1_out2), .address(address[2:0]), .inpt(inpt), .out_5(ram8_3_out_5));
  RAM8 ram8_4 (.clock(clock), .load(demultiplexer_1_out3), .address(address[2:0]), .inpt(inpt), .out_5(ram8_4_out_5));
  RAM8 ram8_5 (.clock(clock), .load(demultiplexer_1_out4), .address(address[2:0]), .inpt(inpt), .out_5(ram8_5_out_5));
  RAM8 ram8_6 (.clock(clock), .load(demultiplexer_1_out5), .address(address[2:0]), .inpt(inpt), .out_5(ram8_6_out_5));
  RAM8 ram8_7 (.clock(clock), .load(demultiplexer_1_out6), .address(address[2:0]), .inpt(inpt), .out_5(ram8_7_out_5));
  RAM8 ram8_8 (.clock(clock), .load(demultiplexer_1_out7), .address(address[2:0]), .inpt(inpt), .out_5(ram8_8_out_5));
  Multiplexer #(.select(3), .width(16)) multiplexer_1 (
    .in0(ram8_1_out_5), .in1(ram8_2_out_5), .in2(ram8_3_out_5), .in3(ram8_4_out_5), .in4(ram8_5_out_5),
    .in5(ram8_6_out_5), .in6(ram8_7_out_5), .in7(ram8_8_out_5), .out(outp), .sel(address[5:3]));
endmodule

module PC (
  input  clock,
  input  inc,
  input  [15:0] inpt,
  input  load,
  input  reset,
  output [15:0] outpt
);

  wire or_1_out, or_2_out;
  wire [15:0] inc16_1_outpt, multiplexer_1_out, multiplexer_2_out, multiplexer_3_out;

  Register #(.width(16)) register_1 (.D(multiplexer_3_out), .en(or_2_out), .clk(clock), .Q(outpt));  // open: clr
  Multiplexer #(.width(16)) multiplexer_1 (.in0(outpt), .in1(inc16_1_outpt), .out(multiplexer_1_out), .sel(inc));
  Inc16 inc16_1 (.inpt(outpt), .outpt(inc16_1_outpt));
  Multiplexer #(.width(16)) multiplexer_2 (.in0(multiplexer_1_out), .in1(inpt), .out(multiplexer_2_out), .sel(load));
  or or_1 (or_1_out, reset, inc);
  Multiplexer #(.width(16)) multiplexer_3 (
    .in0(multiplexer_2_out), .in1({16{1'b0}}), .out(multiplexer_3_out), .sel(reset));
  or or_2 (or_2_out, or_1_out, load);
endmodule

module RAM512 (
  input  load,
  input  [8:0] address,
  input  [15:0] inpt,
  output [15:0] outp
);

  wire demultiplexer_1_out0, demultiplexer_1_out1, demultiplexer_1_out2, demultiplexer_1_out3,
       demultiplexer_1_out4, demultiplexer_1_out5, demultiplexer_1_out6, demultiplexer_1_out7;
  wire [15:0] undriven, undriven_2, undriven_3, undriven_4, undriven_5, undriven_6, undriven_7, undriven_8;

  Demultiplexer #(.select(3)) demultiplexer_1 (
    .out0(demultiplexer_1_out0), .out1(demultiplexer_1_out1), .out2(demultiplexer_1_out2),
    .out3(demultiplexer_1_out3), .out4(demultiplexer_1_out4), .out5(demultiplexer_1_out5),
    .out6(demultiplexer_1_out6), .out7(demultiplexer_1_out7), .in(load), .sel(address[8:6]));
  Multiplexer #(.select(3), .width(16)) multiplexer_1 (
    .in0(undriven), .in1(undriven_7), .in2(undriven_8), .in3(undriven_2), .in4(undriven_3), .in5(undriven_4),
    .in6(undriven_5), .in7(undriven_6), .out(outp), .sel(address[8:6]));
endmodule

module RAM4K (
  input  load,
  input  [11:0] address,
  input  [15:0] inpt,
  output [15:0] outp
);

  wire demultiplexer_1_out0, demultiplexer_1_out1, demultiplexer_1_out2, demultiplexer_1_out3,
       demultiplexer_1_out4, demultiplexer_1_out5, demultiplexer_1_out6, demultiplexer_1_out7;
  wire [15:0] undriven, undriven_2, undriven_3, undriven_4, undriven_5, undriven_6, undriven_7, undriven_8;

  Demultiplexer #(.select(3)) demultiplexer_1 (
    .out0(demultiplexer_1_out0), .out1(demultiplexer_1_out1), .out2(demultiplexer_1_out2),
    .out3(demultiplexer_1_out3), .out4(demultiplexer_1_out4), .out5(demultiplexer_1_out5),
    .out6(demultiplexer_1_out6), .out7(demultiplexer_1_out7), .in(load), .sel(address[11:9]));
  Multiplexer #(.select(3), .width(16)) multiplexer_1 (
    .in0(undriven), .in1(undriven_7), .in2(undriven_8), .in3(undriven_2), .in4(undriven_3), .in5(undriven_4),
    .in6(undriven_5), .in7(undriven_6), .out(outp), .sel(address[11:9]));
endmodule

module RAM16K (
  input  load,
  input  [13:0] address,
  input  [15:0] inpt,
  output [15:0] outp
);

  wire demultiplexer_1_out0, demultiplexer_1_out1, demultiplexer_1_out2, demultiplexer_1_out3;
  wire [15:0] undriven, undriven_2, undriven_3, undriven_4;

  Demultiplexer #(.select(2)) demultiplexer_1 (
    .out0(demultiplexer_1_out0), .out1(demultiplexer_1_out1), .out2(demultiplexer_1_out2),
    .out3(demultiplexer_1_out3), .in(load), .sel(address[13:12]));
  Multiplexer #(.select(2), .width(16)) multiplexer_1 (
    .in0(undriven), .in1(undriven_3), .in2(undriven_4), .in3(undriven_2), .out(outp), .sel(address[13:12]));
endmodule

module Inc16 (
  input  [15:0] inpt,
  output [15:0] outpt
);

  SixteenBitAdder sixteenbitadder_1 (.x(inpt), .y(16'h1), .outp(outpt));  // open: cin, cout
endmodule

module CPU (
  input  [15:0] instruction,
  input  [15:0] inM,
  input  reset,
  output [15:0] outM,
  output writeM,
  output [15:0] addressM,
  output [15:0] pcc,
  output clockOut
);

  wire and_1_out, not_1_out, or_1_out, pccontroler_1_inc, pccontroler_1_load;
  wire [15:0] multiplexer_1_out, multiplexer_2_out, register_2_q;

  Clock clock_1 (.out(clockOut));
  Multiplexer #(.width(16)) multiplexer_1 (
    .in0(instruction), .in1(outM), .out(multiplexer_1_out), .sel(instruction[15]));
  not not_1 (not_1_out, instruction[15]);
  and and_1 (and_1_out, instruction[15], instruction[4]);
  or or_1 (or_1_out, instruction[5], not_1_out);
  Register #(.width(16)) register_1 (.D(multiplexer_1_out), .en(or_1_out), .clk(clockOut), .Q(addressM));  // open: clr
  PCControler pccontroler_1 (
    .inpt(outM), .instruction(instruction), .load(pccontroler_1_load), .inc(pccontroler_1_inc));
  Register #(.width(16)) register_2 (.D(outM), .en(and_1_out), .clk(clockOut), .Q(register_2_q));  // open: clr
  Multiplexer #(.width(16)) multiplexer_2 (.in0(addressM), .in1(inM), .out(multiplexer_2_out), .sel(instruction[12]));
  PC pc_1 (
    .clock(clockOut), .inc(pccontroler_1_inc), .inpt(addressM), .load(pccontroler_1_load), .reset(reset),
    .outpt(pcc));
  ULA ula_1 (
    .x(register_2_q), .y(multiplexer_2_out), .zx(instruction[11]), .nx(instruction[10]), .zy(instruction[9]),
    .ny(instruction[8]), .f(instruction[7]), .no(instruction[6]), .outp(outM));  // open: zr, ng, overflow
  and and_2 (writeM, instruction[15], instruction[3]);
endmodule

module Comparatorr (
  input  [15:0] inpt,
  output eqz,
  output ltz,
  output gtz
);

  wire not_2_out, or16way_1_out_2;

  not not_1 (eqz, or16way_1_out_2);
  Or16Way or16way_1 (.in_1(inpt), .out_2(or16way_1_out_2));
  and and_1 (ltz, inpt[15], 1'b1);
  not not_2 (not_2_out, ltz);
  and and_2 (gtz, not_2_out, or16way_1_out_2);
endmodule

module PCControler (
  input  [15:0] inpt,
  input  [15:0] instruction,
  output load,
  output inc
);

  wire and_1_out, and_2_out, and_3_out, comparatorr_1_eqz, comparatorr_1_gtz, comparatorr_1_ltz, or_1_out,
       or_2_out;

  Comparatorr comparatorr_1 (.inpt(inpt), .eqz(comparatorr_1_eqz), .ltz(comparatorr_1_ltz), .gtz(comparatorr_1_gtz));
  and and_1 (and_1_out, comparatorr_1_eqz, instruction[1]);
  and and_2 (and_2_out, comparatorr_1_ltz, instruction[2]);
  and and_3 (and_3_out, comparatorr_1_gtz, instruction[0]);
  or or_1 (or_1_out, and_1_out, and_2_out);
  or or_2 (or_2_out, or_1_out, and_3_out);
  and and_4 (load, or_2_out, instruction[15]);
  not not_1 (inc, load);
endmodule

module Memory (
  input  load,
  input  [15:0] inpt,
  input  [14:0] address,
  input  clock,
  input  [15:0] keyboard,
  output [15:0] outt
);

  wire and_1_out, and_2_out, and_3_out, and_4_out, multiplexer_1_out, multiplexer_2_out, not_1_out,
       not_2_out, or_1_out, or_2_out, or_3_out;
  wire [15:0] multiplexer_3_out, screen_2_dout, screen_dout;

  and and_1 (and_1_out, 1'b1, inpt[14]);
  or or_1 (or_1_out, address[0], address[1], address[2], address[3], address[4], address[5], address[6], address[7]);
  or or_2 (or_2_out, address[8], address[9], address[10], address[11], address[12]);
  Multiplexer multiplexer_1 (.in0(load), .out(multiplexer_1_out), .sel(and_1_out));  // open: in1
  or or_3 (or_3_out, or_1_out, or_2_out);
  and and_2 (and_2_out, address[13], and_1_out);
  and and_3 (and_3_out, and_2_out, not_1_out);
  not not_1 (not_1_out, or_3_out);
  RAM #(.addrWidth(14), .dataWidth(16)) screen (
    .addr(address[13:0]), .we(multiplexer_1_out), .oe(1'b1), .clk(clock), .din(inpt), .dout(screen_dout));
  not not_2 (not_2_out, and_3_out);
  and and_4 (and_4_out, not_2_out, and_1_out);
  Multiplexer multiplexer_2 (.in1(load), .out(multiplexer_2_out), .sel(and_4_out));  // open: in0
  RAM #(.addrWidth(14), .dataWidth(16)) screen_2 (
    .addr(address[13:0]), .we(multiplexer_2_out), .oe(1'b1), .clk(clock), .din(inpt), .dout(screen_2_dout));
  Multiplexer #(.width(16)) multiplexer_3 (
    .in0(screen_2_dout), .in1(keyboard), .out(multiplexer_3_out), .sel(and_3_out));
  Multiplexer #(.width(16)) multiplexer_4 (.in0(screen_dout), .in1(multiplexer_3_out), .out(outt), .sel(address[14]));
endmodule
